# Fritzing sketch TidePoolProposed (saved by Fritzing 0.9.3b)

parts:
  LED1 = RGB LED (com. cathode, rgb) [package="5 mm [THT]"]
  U4 = RELAY [package=relay-t9a-2]
  U5 = SPM0204UD5 [package=spm0204ud5]
  Part3 = DeuLigne 1.1 - The Snootlab's LCD shield for Arduino  # not connected
  U3 = RELAY [package=relay-t9a-2]
  Part2 = Arduino Uno (Rev3) - ICSP

nets (from the schematic view):
  GND: LED1.common_cathode, U4.COIL2, U5.GND, U3.COIL2, Part2.GND
  N1: LED1.green_anode, Part2.D9_PWM
  N2: LED1.blue_anode, Part2.D10_PWM/SS
  N3: U4.COIL1, Part2.D12/MISO
  pump1: U4.MAIN
  GND_2: U4.NC, U3.NC
  120V: U4.NO, U3.NO
  N4: U5.OUT, Part2.D3_PWM
  N5: U5.GND#, Part2.D2
  N6: U5.VS, Part2.5V
  N7: U3.COIL1, Part2.D11_PWM/MOSI
  pump2: U3.MAIN

notes:
  pump1
  pump2
  ultrasonic sensor
